# Fritzing sketch sensors (saved by Fritzing 0.9.4)
circuit board: 7cm x 5cm

parts:
  Mod1 = MQ-7 breakout
  TD-er1 = MH-Z19 CO2 sensor [part_number=MH-Z19]
  J1 = female pin header, 1 pin [form="♀ (female)"]
  J2 = female pin header, 1 pin [form="♀ (female)"]
  J3 = female pin header, 19 pins [form="♀ (female)"]
  J4 = female pin header, 19 pins [form="♀ (female)"]
  U1 = ESP32-38PinWide [part_number=ESP32-38PinWide]
  R1 = Resistor [tolerance=±5% resistance=1.3k package=THT]
  R2 = Resistor [tolerance=±5% resistance=2k package=THT]

nets:
  VIN: Mod1.VCC, TD-er1.Vin, J2.pin1, J4.pin1, U1.VIN
  GND: Mod1.GND, TD-er1.GND, J1.pin1, J3.pin19, U1.GND, R2.Pin_1
  N1: Mod1.AO, R1.Pin_0
  N2: TD-er1.RX, U1.GPIO12
  N3: TD-er1.TX, U1.GPIO13
  N4: J3.pin1, U1.GPIO6
  N5: J4.pin19, U1.3.3
  N6: U1.GPIO32, R1.Pin_1, R2.Pin_0

custom parts:
  MQ-7 breakout: MQ-5 gas sensor
  ESP32-38PinWide: Generic 38-Pin ESP32 with wide format (only access to one side of pins on a breadboard) based on Stephen Lilley's HiLetgo ESP-WROOM-32 ESP32 ESP-32S Development Board.
